// Logisim project JojoMemory.circ as structural Verilog: 15 circuits, main circuit main
module main (
);

  wire _0_out, _1_out, _2_out, _3_out, _4_out, _5_out, _6_out, _7_out, _8_out, _9_out, button_2_out,
       button_out, Clock, dead, decoder_1_out0, decoder_1_out1, decoder_1_out2, decoder_1_out3, enter, match,
       not_1_out, undriven, undriven_2, undriven_3, undriven_4;
  wire [1:0] digit_selector_digit_place;
  wire [2:0] BC_match_calculator_bulls, BC_match_calculator_cows, state, wins_lives_memory_lives;
  wire [3:0] bit_extender_1_out, bit_extender_2_out, bit_extender_3_out, D0, D1, D2, D3, I0, I1, I2, I3, S0,
       S1, S2, S3, T0, T1, T2, T3, wins_lives_memory_wins;

  Button _1 (.out(_1_out));
  Button _4 (.out(_4_out));
  Button _7 (.out(_7_out));
  Button button (.out(button_out));
  Button _2 (.out(_2_out));
  Button _3 (.out(_3_out));
  Button _5 (.out(_5_out));
  Button _6 (.out(_6_out));
  Button _8 (.out(_8_out));
  Button _9 (.out(_9_out));
  Button _0 (.out(_0_out));
  Button button_2 (.out(button_2_out));
  Button u_Enter (.out(enter));
  digit_selector digit_selector (
    .L(button_out), .R(button_2_out), .clock(Clock), .state(state), .Digit_Place(digit_selector_digit_place));
  digit_input number_input (
    ._0(_0_out), ._1(_1_out), ._2(_2_out), ._3(_3_out), ._4(_4_out), ._5(_5_out), ._6(_6_out), ._7(_7_out),
    ._8(_8_out), ._9(_9_out), .clock(Clock), .in_12(digit_selector_digit_place), .State(state), .I0(I0),
    .I1(I1), .I2(I2), .I3(I3));
  store_memory setup_digits (
    .I0(I0), .I1(I1), .I2(I2), .I3(I3), .Enter(enter), .state(state), .clock(Clock), .s0(S0), .s1(S1),
    .s2(S2), .s3(S3));
  try_memory test_digits (
    .I0(I0), .I1(I1), .I2(I2), .I3(I3), .Enter(enter), .state(state), .clock(Clock), .tr0(T0), .tr1(T1),
    .tr2(T2), .tr3(T3));
  digit_display digit_display_picker (
    .I0(I0), .I1(I1), .I2(I2), .I3(I3), .S0(S0), .S1(S1), .S2(S2), .S3(S3), .state(state), .D0(D0), .D1(D1),
    .D2(D2), .D3(D3));
  Decoder #(.select(2)) decoder_1 (
    .out0(decoder_1_out0), .out1(decoder_1_out1), .out2(decoder_1_out2), .out3(decoder_1_out3),
    .sel(digit_selector_digit_place));  // open: en
  LED led_1 (.in(decoder_1_out3));
  Hex_Digit_Display hex_digit_display_1 (.value(D3));  // open: dp
  // Probe on state
  mik_state_controller state_control (.dead(dead), .win(match), .enter(enter), .Clock(Clock), .state(state));
  LED led_2 (.in(decoder_1_out2));
  Hex_Digit_Display hex_digit_display_2 (.value(D2));  // open: dp
  LED led_3 (.in(decoder_1_out0));
  LED led_4 (.in(decoder_1_out1));
  Hex_Digit_Display hex_digit_display_3 (.value(D0));  // open: dp
  Hex_Digit_Display hex_digit_display_4 (.value(D1));  // open: dp
  Clock clock_1 (.out(Clock));
  Hex_Digit_Display hex_digit_display_5 (.value(S3));  // open: dp
  Hex_Digit_Display hex_digit_display_6 (.value(S1));  // open: dp
  Hex_Digit_Display hex_digit_display_7 (.value(S2));  // open: dp
  match_calculator BC_match_calculator (
    .I0(T0), .I1(T1), .I2(T2), .I3(T3), .S0(S0), .S1(S1), .S2(S2), .S3(S3), .state(state), .match(match),
    .bulls(BC_match_calculator_bulls), .cows(BC_match_calculator_cows));
  LED Win (.in(undriven));
  LED Lose (.in(not_1_out));
  not not_1 (not_1_out, undriven);
  LED Start (.in(undriven_2));
  LED Game (.in(undriven_3));
  LED Wait (.in(undriven_4));
  wins_lives_memory wins_lives_memory (
    .match(match), .state(state), .clock(Clock), .wins(wins_lives_memory_wins),
    .lives(wins_lives_memory_lives));
  Hex_Digit_Display hex_digit_display_8 (.value(S0));  // open: dp
  Hex_Digit_Display hex_digit_display_9 (.value(bit_extender_1_out));  // open: dp
  assign bit_extender_1_out = {{1{1'b0}}, BC_match_calculator_bulls};  // Bit_Extender bit_extender_1
  assign bit_extender_2_out = {{1{1'b0}}, BC_match_calculator_cows};  // Bit_Extender bit_extender_2
  Hex_Digit_Display hex_digit_display_10 (.value(wins_lives_memory_wins));  // open: dp
  Hex_Digit_Display hex_digit_display_11 (.value(bit_extender_3_out));  // open: dp
  assign bit_extender_3_out = {{1{1'b0}}, wins_lives_memory_lives};  // Bit_Extender bit_extender_3
  and and_1 (dead, wins_lives_memory_lives[0], ~wins_lives_memory_lives[1], ~wins_lives_memory_lives[2]);  // AND_Gate
  Hex_Digit_Display hex_digit_display_12 (.value(bit_extender_2_out));  // open: dp

  // Notes on the sheet:
  //   Inputs
  //   Saved Setup Digits
  //   Bulls
  //   Cows
  //   Wins
  //   Lives
endmodule

// digits_memory
module saved_digits_memory (
  input  [3:0] I0,
  input  [3:0] I1,
  input  [3:0] I2,
  input  [3:0] I3,
  input  Enter,
  input  clock,
  input  [2:0] state,
  output [3:0] S0,
  output [3:0] S1,
  output [3:0] S2,
  output [3:0] S3,
  output [3:0] D0,
  output [3:0] D1,
  output [3:0] D2,
  output [3:0] D3
);

  wire and_1_out, nand_1_out;
  wire [3:0] controlled_buffer_1_out, controlled_buffer_2_out, controlled_buffer_3_out,
       controlled_buffer_4_out;

  and and_1 (and_1_out, ~state[0], ~state[1], ~state[2], Enter);  // AND_Gate
  assign controlled_buffer_1_out = and_1_out ? I0 : 4'bz;  // Controlled_Buffer controlled_buffer_1
  assign controlled_buffer_2_out = and_1_out ? I1 : 4'bz;  // Controlled_Buffer controlled_buffer_2
  assign controlled_buffer_3_out = and_1_out ? I2 : 4'bz;  // Controlled_Buffer controlled_buffer_3
  assign controlled_buffer_4_out = and_1_out ? I3 : 4'bz;  // Controlled_Buffer controlled_buffer_4
  Register #(.width(4)) register_1 (.D(controlled_buffer_1_out), .Q(S0), .clk(clock));  // open: en, clr
  Register #(.width(4)) register_2 (.D(controlled_buffer_2_out), .Q(S1), .clk(clock));  // open: en, clr
  Register #(.width(4)) register_3 (.D(controlled_buffer_3_out), .Q(S2), .clk(clock));  // open: en, clr
  Register #(.width(4)) register_4 (.D(controlled_buffer_4_out), .Q(S3), .clk(clock));  // open: en, clr
  nand nand_1 (nand_1_out, state[0], ~state[1], state[2]);  // NAND_Gate
  // Probe on {D3, D2, D1, D0}
  Multiplexer #(.width(16), .enable("false")) multiplexer_1 (
    .in0({S3, S2, S1, S0}), .in1({I3, I2, I1, I0}), .out({D3, D2, D1, D0}), .sel(nand_1_out));
endmodule

module digit_input (
  input  _0,
  input  _1,
  input  _2,
  input  _3,
  input  _4,
  input  _5,
  input  _6,
  input  _7,
  input  _8,
  input  _9,
  input  clock,
  input  [1:0] in_12,
  input  [2:0] State,
  output [3:0] I0,
  output [3:0] I1,
  output [3:0] I2,
  output [3:0] I3
);

  wire and_1_out, and_2_out, and_3_out, and_4_out, and_5_out, and_6_out, and_7_out, and_8_out, and_9_out,
       decoder_1_out0, decoder_1_out1, decoder_1_out2, decoder_1_out3, or_1_out, or_2_out,
       priority_encoder_1_gs;
  wire [3:0] priority_encoder_1_out;

  Priority_Encoder #(.select(4)) priority_encoder_1 (
    .in0(_0), .in1(_1), .in2(_2), .in3(_3), .in4(_4), .in5(_5), .in6(_6), .in7(_7), .in8(_8), .in9(_9),
    .out(priority_encoder_1_out), .gs(priority_encoder_1_gs));  // open: in10, in11, in12, in13, in14, in15, en_out, en_in
  // Probe on priority_encoder_1_out
  Decoder #(.select(2)) decoder_1 (
    .out0(decoder_1_out0), .out1(decoder_1_out1), .out2(decoder_1_out2), .out3(decoder_1_out3), .sel(in_12));  // open: en
  Register #(.width(4)) register_1 (.D(priority_encoder_1_out), .en(and_3_out), .Q(I0), .clk(clock), .clr(or_1_out));
  Register #(.width(4)) register_2 (.D(priority_encoder_1_out), .en(and_4_out), .Q(I1), .clk(clock), .clr(or_1_out));
  Register #(.width(4)) register_3 (.D(priority_encoder_1_out), .en(and_5_out), .Q(I2), .clk(clock), .clr(or_1_out));
  Register #(.width(4)) register_4 (.D(priority_encoder_1_out), .en(and_6_out), .Q(I3), .clk(clock), .clr(or_1_out));
  or or_1 (or_1_out, and_1_out, and_7_out);
  and and_1 (and_1_out, State[2], State[1], State[0]);
  and and_2 (and_2_out, or_2_out, priority_encoder_1_gs);
  and and_3 (and_3_out, and_2_out, decoder_1_out0);
  and and_4 (and_4_out, and_2_out, decoder_1_out1);
  and and_5 (and_5_out, and_2_out, decoder_1_out2);
  and and_6 (and_6_out, and_2_out, decoder_1_out3);
  and and_7 (and_7_out, ~State[2], State[1], ~State[0]);  // AND_Gate
  or or_2 (or_2_out, and_8_out, and_9_out);
  and and_8 (and_8_out, ~State[2], ~State[1], ~State[0]);  // AND_Gate
  and and_9 (and_9_out, ~State[2], State[1], State[0]);  // AND_Gate

  // Other names for the same wires on the sheet: Clock_T = clock
endmodule

module bulls_calculator (
  input  [3:0] I0,
  input  [3:0] I1,
  input  [3:0] I2,
  input  [3:0] I3,
  input  [3:0] S0,
  input  [3:0] S1,
  input  [3:0] S2,
  input  [3:0] S3,
  output [2:0] bulls
);

  wire comparator_1_eq, comparator_2_eq, comparator_3_eq, comparator_4_eq;

  Comparator #(.width(4)) comparator_1 (.a(I0), .b(S0), .eq(comparator_1_eq));  // open: gt, lt
  Comparator #(.width(4)) comparator_2 (.a(I1), .b(S1), .eq(comparator_2_eq));  // open: gt, lt
  Comparator #(.width(4)) comparator_3 (.a(I2), .b(S2), .eq(comparator_3_eq));  // open: gt, lt
  Comparator #(.width(4)) comparator_4 (.a(I3), .b(S3), .eq(comparator_4_eq));  // open: gt, lt
  BitAdder #(.width(1)) bitadder_1 (
    .in0(comparator_1_eq), .in1(comparator_2_eq), .in2(comparator_3_eq), .in3(comparator_4_eq), .out(bulls));
endmodule

module wins_lives_memory (
  input  match,
  input  clock,
  input  [2:0] state,
  output [3:0] wins,
  output [2:0] lives
);

  wire and_1_out, and_2_out, and_3_out;
  wire [2:0] subtractor_1_out;
  wire [3:0] adder_1_out;

  Adder #(.width(4)) adder_1 (.a(wins), .b(4'b0001), .out(adder_1_out));  // open: cin, cout
  and and_1 (and_1_out, match, and_2_out);
  Subtractor #(.width(3)) subtractor_1 (.a(lives), .b(3'b001), .out(subtractor_1_out));  // open: bin, bout
  and and_2 (and_2_out, ~state[0], ~state[1], state[2]);  // AND_Gate
  Register #(.width(4)) u_wins (.D(adder_1_out), .en(and_1_out), .Q(wins), .clk(clock));  // open: clr
  D_Flip_Flop d_ff_1 (
    .clk(clock), .D(subtractor_1_out[0]), .Q(lives[0]), .preset(and_3_out), .en(and_2_out));  // open: Qn, reset
  D_Flip_Flop d_ff_2 (
    .clk(clock), .D(subtractor_1_out[1]), .Q(lives[1]), .preset(and_3_out), .en(and_2_out));  // open: Qn, reset
  D_Flip_Flop d_ff_3 (
    .clk(clock), .D(subtractor_1_out[2]), .Q(lives[2]), .preset(and_3_out), .en(and_2_out));  // open: Qn, reset
  and and_3 (and_3_out, ~state[0], ~state[1], ~state[2]);  // AND_Gate
endmodule

module cows_calculator (
  input  [3:0] I0,
  input  [3:0] I1,
  input  [3:0] I2,
  input  [3:0] I3,
  input  [3:0] S0,
  input  [3:0] S1,
  input  [3:0] S2,
  input  [3:0] S3,
  output [2:0] cows
);

  wire comparator_1_eq, comparator_2_eq, comparator_3_eq, comparator_4_eq, comparator_5_eq, comparator_6_eq,
       comparator_7_eq, comparator_8_eq, comparator_9_eq, comparator_10_eq, comparator_11_eq,
       comparator_12_eq, or_1_out, or_2_out, or_3_out, or_4_out;

  Comparator #(.width(4)) comparator_1 (.a(I1), .b(S0), .eq(comparator_1_eq));  // open: gt, lt
  Comparator #(.width(4)) comparator_2 (.a(I2), .b(S0), .eq(comparator_2_eq));  // open: gt, lt
  Comparator #(.width(4)) comparator_3 (.a(I3), .b(S0), .eq(comparator_3_eq));  // open: gt, lt
  Comparator #(.width(4)) comparator_4 (.a(I0), .b(S1), .eq(comparator_4_eq));  // open: gt, lt
  Comparator #(.width(4)) comparator_5 (.a(I2), .b(S1), .eq(comparator_5_eq));  // open: gt, lt
  Comparator #(.width(4)) comparator_6 (.a(I3), .b(S1), .eq(comparator_6_eq));  // open: gt, lt
  Comparator #(.width(4)) comparator_7 (.a(I0), .b(S2), .eq(comparator_7_eq));  // open: gt, lt
  Comparator #(.width(4)) comparator_8 (.a(I1), .b(S2), .eq(comparator_8_eq));  // open: gt, lt
  Comparator #(.width(4)) comparator_9 (.a(I3), .b(S2), .eq(comparator_9_eq));  // open: gt, lt
  Comparator #(.width(4)) comparator_10 (.a(I0), .b(S3), .eq(comparator_10_eq));  // open: gt, lt
  Comparator #(.width(4)) comparator_11 (.a(I1), .b(S3), .eq(comparator_11_eq));  // open: gt, lt
  Comparator #(.width(4)) comparator_12 (.a(I2), .b(S3), .eq(comparator_12_eq));  // open: gt, lt
  or or_1 (or_1_out, comparator_1_eq, comparator_2_eq, comparator_3_eq);
  or or_2 (or_2_out, comparator_4_eq, comparator_5_eq, comparator_6_eq);
  or or_3 (or_3_out, comparator_7_eq, comparator_8_eq, comparator_9_eq);
  or or_4 (or_4_out, comparator_10_eq, comparator_11_eq, comparator_12_eq);
  BitAdder #(.width(1)) bitadder_1 (.in0(or_1_out), .in1(or_2_out), .in2(or_3_out), .in3(or_4_out), .out(cows));
endmodule

module match_calculator (
  input  [3:0] I0,
  input  [3:0] I1,
  input  [3:0] I2,
  input  [3:0] I3,
  input  [3:0] S0,
  input  [3:0] S1,
  input  [3:0] S2,
  input  [3:0] S3,
  input  [2:0] state,
  output match,
  output [2:0] bulls,
  output [2:0] cows
);

  wire and_1_out;
  wire [2:0] bulls_calculator_1_bulls, cows_calculator_1_cows;

  bulls_calculator bulls_calculator_1 (
    .I0(I0), .I1(I1), .I2(I2), .I3(I3), .S0(S0), .S1(S1), .S2(S2), .S3(S3), .bulls(bulls_calculator_1_bulls));
  cows_calculator cows_calculator_1 (
    .I0(I0), .I1(I1), .I2(I2), .I3(I3), .S0(S0), .S1(S1), .S2(S2), .S3(S3), .cows(cows_calculator_1_cows));
  Comparator #(.width(3)) comparator_1 (.a(bulls_calculator_1_bulls), .b(3'b100), .eq(match));  // open: gt, lt
  assign bulls = and_1_out ? bulls_calculator_1_bulls : 3'bz;  // Controlled_Buffer controlled_buffer_1
  assign cows = and_1_out ? cows_calculator_1_cows : 3'bz;  // Controlled_Buffer controlled_buffer_2
  and and_1 (and_1_out, state[0], state[1], ~state[2]);  // AND_Gate
endmodule

module digit_display (
  input  [3:0] I0,
  input  [3:0] I1,
  input  [3:0] I2,
  input  [3:0] I3,
  input  [3:0] S0,
  input  [3:0] S1,
  input  [3:0] S2,
  input  [3:0] S3,
  input  [2:0] state,
  output [3:0] D0,
  output [3:0] D1,
  output [3:0] D2,
  output [3:0] D3
);

  wire and_1_out, and_2_out, or_1_out, xnor_1_out;

  and and_1 (and_1_out, ~state[0], state[1], state[2]);  // AND_Gate
  and and_2 (and_2_out, state[0], ~state[1], state[2]);  // AND_Gate
  xnor xnor_1 (xnor_1_out, state[0], state[1], state[2]);
  // Probe on {D3, D2, D1, D0}
  Multiplexer #(.width(16)) multiplexer_1 (
    .in0({I3, I2, I1, I0}), .in1({S3, S2, S1, S0}), .out({D3, D2, D1, D0}), .sel(or_1_out), .en(xnor_1_out));
  or or_1 (or_1_out, and_1_out, and_2_out);
endmodule

module store_memory (
  input  [3:0] I0,
  input  [3:0] I1,
  input  [3:0] I2,
  input  [3:0] I3,
  input  Enter,
  input  clock,
  input  [2:0] state,
  output [3:0] s0,
  output [3:0] s1,
  output [3:0] s2,
  output [3:0] s3
);

  wire and_1_out;

  and and_1 (and_1_out, Enter, ~state[2], ~state[1], ~state[0]);  // AND_Gate
  Register #(.width(4)) register_1 (.D(I0), .en(and_1_out), .Q(s0), .clk(clock));  // open: clr
  Register #(.width(4)) register_2 (.D(I1), .en(and_1_out), .Q(s1), .clk(clock));  // open: clr
  Register #(.width(4)) register_3 (.D(I2), .en(and_1_out), .Q(s2), .clk(clock));  // open: clr
  Register #(.width(4)) register_4 (.D(I3), .en(and_1_out), .Q(s3), .clk(clock));  // open: clr
endmodule

module try_memory (
  input  [3:0] I0,
  input  [3:0] I1,
  input  [3:0] I2,
  input  [3:0] I3,
  input  Enter,
  input  clock,
  input  [2:0] state,
  output [3:0] tr0,
  output [3:0] tr1,
  output [3:0] tr2,
  output [3:0] tr3
);

  wire and_1_out;

  and and_1 (and_1_out, Enter, ~state[2], state[1], state[0]);  // AND_Gate
  Register #(.width(4)) register_1 (.D(I0), .en(and_1_out), .Q(tr0), .clk(clock));  // open: clr
  Register #(.width(4)) register_2 (.D(I1), .en(and_1_out), .Q(tr1), .clk(clock));  // open: clr
  Register #(.width(4)) register_3 (.D(I2), .en(and_1_out), .Q(tr2), .clk(clock));  // open: clr
  Register #(.width(4)) register_4 (.D(I3), .en(and_1_out), .Q(tr3), .clk(clock));  // open: clr
endmodule

module digit_selector (
  input  L,
  input  R,
  input  clock,
  input  [2:0] state,
  output [1:0] Digit_Place
);

  wire and_1_out, and_2_out, nor_1_out, or_1_out, xor_1_out;
  wire [1:0] adder_1_out, multiplexer_1_out, subtractor_1_out;

  nor nor_1 (nor_1_out, state[2], state[1], state[0]);
  xor xor_1 (xor_1_out, L, R);
  and and_1 (and_1_out, ~state[2], state[1], state[0]);  // AND_Gate
  Adder #(.width(2)) adder_1 (.a(Digit_Place), .b(2'b01), .out(adder_1_out));  // open: cin, cout
  Subtractor #(.width(2)) subtractor_1 (.a(Digit_Place), .b(2'b01), .out(subtractor_1_out));  // open: bin, bout
  and and_2 (and_2_out, xor_1_out, or_1_out);
  or or_1 (or_1_out, nor_1_out, and_1_out);
  Multiplexer #(.width(2), .enable("false")) multiplexer_1 (
    .in0(adder_1_out), .in1(subtractor_1_out), .out(multiplexer_1_out), .sel(R));
  Register #(.width(2)) register_1 (.D(multiplexer_1_out), .en(and_2_out), .Q(Digit_Place), .clk(clock));  // open: clr
endmodule

module mik_state_controller (
  input  dead,
  input  win,
  input  enter,
  input  Clock,
  output [2:0] state
);

  wire and_1_out, and_2_out, and_3_out, and_4_out, and_5_out, and_6_out, and_7_out, and_8_out, and_9_out,
       and_10_out, and_11_out, and_12_out, and_13_out, and_14_out, not_1_out, not_2_out, not_3_out,
       not_4_out, not_5_out, not_6_out, not_7_out, not_8_out, not_9_out, not_10_out, not_11_out, not_12_out,
       not_13_out, not_14_out, not_15_out, not_16_out, not_17_out, not_18_out, not_19_out, not_20_out,
       not_21_out, or_1_out, or_2_out, or_3_out;

  not not_1 (not_1_out, state[1]);
  not not_2 (not_2_out, state[0]);
  not not_3 (not_3_out, state[2]);
  not not_4 (not_4_out, state[1]);
  not not_5 (not_5_out, state[1]);
  not not_6 (not_6_out, enter);
  not not_7 (not_7_out, state[2]);
  not not_8 (not_8_out, enter);
  not not_9 (not_9_out, state[2]);
  not not_10 (not_10_out, dead);
  not not_11 (not_11_out, win);
  not not_12 (not_12_out, state[1]);
  not not_13 (not_13_out, state[0]);
  not not_14 (not_14_out, state[1]);
  not not_15 (not_15_out, state[0]);
  not not_16 (not_16_out, enter);
  not not_17 (not_17_out, state[2]);
  not not_18 (not_18_out, enter);
  not not_19 (not_19_out, state[1]);
  not not_20 (not_20_out, state[0]);
  not not_21 (not_21_out, state[0]);
  and and_1 (and_1_out, state[2], not_1_out, state[0]);
  and and_2 (and_2_out, state[2], state[1], not_2_out);
  and and_3 (and_3_out, enter, not_3_out, state[1], state[0]);
  and and_4 (and_4_out, win, state[2], not_4_out);
  and and_5 (and_5_out, dead, state[2], not_5_out);
  and and_6 (and_6_out, not_6_out, not_7_out, state[0]);
  and and_7 (and_7_out, not_8_out, not_9_out, state[1]);
  and and_8 (and_8_out, not_10_out, not_11_out, state[2], not_12_out, not_13_out);
  and and_9 (and_9_out, enter, not_14_out, state[0]);
  and and_10 (and_10_out, enter, state[1], not_15_out);
  and and_11 (and_11_out, not_16_out, not_17_out, state[1]);
  and and_12 (and_12_out, not_18_out, state[2], not_19_out);
  and and_13 (and_13_out, state[2], not_20_out);
  and and_14 (and_14_out, enter, not_21_out);
  or or_1 (or_1_out, and_1_out, and_2_out, and_3_out, and_4_out, and_5_out);
  or or_2 (or_2_out, and_6_out, and_7_out, and_8_out, and_9_out, and_10_out);
  or or_3 (or_3_out, and_11_out, and_12_out, and_13_out, and_14_out);
  D_Flip_Flop D3 (.clk(Clock), .D(or_1_out), .Q(state[2]));  // open: Qn, preset, en, reset
  D_Flip_Flop D2 (.clk(Clock), .D(or_2_out), .Q(state[1]));  // open: Qn, preset, en, reset
  D_Flip_Flop D1 (.clk(Clock), .D(or_3_out), .Q(state[0]));  // open: Qn, preset, en, reset
endmodule

module cows_with_display_toggle (
  input  [3:0] tr1,
  input  [3:0] tr2,
  input  [3:0] tr3,
  input  [3:0] tr4,
  input  [3:0] sr1,
  input  [3:0] sr2,
  input  [3:0] sr3,
  input  [3:0] sr4,
  input  [2:0] state,
  output [3:0] Cows
);

  wire and_1_out, comparator_1_eq, comparator_2_eq, comparator_3_eq, comparator_4_eq, comparator_5_eq,
       comparator_6_eq, comparator_7_eq, comparator_8_eq, comparator_9_eq, comparator_10_eq,
       comparator_11_eq, comparator_12_eq, or_1_out, or_2_out, or_3_out, or_4_out;
  wire [2:0] bitadder_1_out;
  wire [3:0] bit_extender_1_out;

  Comparator #(.width(4)) comparator_1 (.a(tr1), .b(sr2), .eq(comparator_1_eq));  // open: gt, lt
  Comparator #(.width(4)) comparator_2 (.a(tr2), .b(sr1), .eq(comparator_2_eq));  // open: gt, lt
  Comparator #(.width(4)) comparator_3 (.a(tr3), .b(sr1), .eq(comparator_3_eq));  // open: gt, lt
  Comparator #(.width(4)) comparator_4 (.a(tr4), .b(sr1), .eq(comparator_4_eq));  // open: gt, lt
  Comparator #(.width(4)) comparator_5 (.a(tr1), .b(sr3), .eq(comparator_5_eq));  // open: gt, lt
  Comparator #(.width(4)) comparator_6 (.a(tr2), .b(sr3), .eq(comparator_6_eq));  // open: gt, lt
  Comparator #(.width(4)) comparator_7 (.a(tr3), .b(sr2), .eq(comparator_7_eq));  // open: gt, lt
  Comparator #(.width(4)) comparator_8 (.a(tr4), .b(sr2), .eq(comparator_8_eq));  // open: gt, lt
  Comparator #(.width(4)) comparator_9 (.a(tr4), .b(sr3), .eq(comparator_9_eq));  // open: gt, lt
  Comparator #(.width(4)) comparator_10 (.a(tr1), .b(sr4), .eq(comparator_10_eq));  // open: gt, lt
  Comparator #(.width(4)) comparator_11 (.a(tr2), .b(sr4), .eq(comparator_11_eq));  // open: gt, lt
  Comparator #(.width(4)) comparator_12 (.a(tr3), .b(sr4), .eq(comparator_12_eq));  // open: gt, lt
  or or_1 (or_1_out, comparator_4_eq, comparator_8_eq, comparator_9_eq);
  or or_2 (or_2_out, comparator_1_eq, comparator_5_eq, comparator_10_eq);
  or or_3 (or_3_out, comparator_2_eq, comparator_6_eq, comparator_11_eq);
  or or_4 (or_4_out, comparator_3_eq, comparator_7_eq, comparator_12_eq);
  BitAdder #(.width(1)) bitadder_1 (
    .in0(or_2_out), .in1(or_3_out), .in2(or_4_out), .in3(or_1_out), .out(bitadder_1_out));
  assign bit_extender_1_out = {{1{1'b0}}, bitadder_1_out};  // Bit_Extender bit_extender_1
  assign Cows = and_1_out ? bit_extender_1_out : 4'bz;  // Controlled_Buffer controlled_buffer_1
  and and_1 (and_1_out, ~state[2], state[1], state[0]);  // AND_Gate
endmodule

module bulls_with_display_toggle (
  input  [3:0] tr1,
  input  [3:0] tr2,
  input  [3:0] tr3,
  input  [3:0] tr4,
  input  [3:0] sr1,
  input  [3:0] sr2,
  input  [3:0] sr3,
  input  [3:0] sr4,
  input  [2:0] state,
  output [3:0] Bulls,
  output match
);

  wire and_1_out, comparator_1_eq, comparator_2_eq, comparator_3_eq, comparator_4_eq;
  wire [2:0] bitadder_1_out;
  wire [3:0] bit_extender_1_out;

  Comparator #(.width(4)) comparator_1 (.a(sr1), .b(tr1), .eq(comparator_1_eq));  // open: gt, lt
  Comparator #(.width(4)) comparator_2 (.a(sr2), .b(tr2), .eq(comparator_2_eq));  // open: gt, lt
  Comparator #(.width(4)) comparator_3 (.a(sr3), .b(tr3), .eq(comparator_3_eq));  // open: gt, lt
  Comparator #(.width(4)) comparator_4 (.a(sr4), .b(tr4), .eq(comparator_4_eq));  // open: gt, lt
  BitAdder #(.width(1)) bitadder_1 (
    .in0(comparator_1_eq), .in1(comparator_2_eq), .in2(comparator_3_eq), .in3(comparator_4_eq),
    .out(bitadder_1_out));
  assign bit_extender_1_out = {{1{1'b0}}, bitadder_1_out};  // Bit_Extender bit_extender_1
  Comparator #(.width(4)) comparator_5 (.a(bit_extender_1_out), .b(4'b0100), .eq(match));  // open: gt, lt
  assign Bulls = and_1_out ? bit_extender_1_out : 4'bz;  // Controlled_Buffer controlled_buffer_1
  and and_1 (and_1_out, ~state[2], state[1], state[0]);  // AND_Gate
endmodule

module state_to_led_decoder (
  input  [2:0] state,
  input  match,
  output start,
  output game,
  output \wait ,
  output win,
  output lose
);

  wire and_1_out, and_2_out, and_3_out, and_4_out, and_5_out, and_6_out, and_7_out, and_8_out, not_1_out,
       not_2_out, not_3_out, not_4_out, not_5_out, not_6_out, not_7_out, not_8_out, not_9_out, not_10_out,
       not_11_out, not_12_out, not_13_out, or_4_out;

  not not_1 (not_1_out, state[2]);
  not not_2 (not_2_out, state[1]);
  not not_3 (not_3_out, state[2]);
  not not_4 (not_4_out, state[0]);
  not not_5 (not_5_out, state[2]);
  not not_6 (not_6_out, state[1]);
  not not_7 (not_7_out, state[0]);
  not not_8 (not_8_out, state[2]);
  not not_9 (not_9_out, state[1]);
  not not_10 (not_10_out, state[0]);
  not not_11 (not_11_out, state[1]);
  not not_12 (not_12_out, state[0]);
  and and_1 (and_1_out, not_1_out, not_2_out);
  and and_2 (and_2_out, not_3_out, not_4_out);
  and and_3 (and_3_out, not_5_out, state[1], state[0]);
  and and_4 (and_4_out, state[2], not_6_out, not_7_out);
  and and_5 (and_5_out, not_8_out, not_9_out, state[0]);
  and and_6 (and_6_out, state[2], not_10_out);
  and and_7 (and_7_out, state[2], not_11_out, state[0]);
  and and_8 (and_8_out, state[2], state[1], not_12_out);
  or or_1 (start, and_1_out, and_2_out);
  or or_2 (game, and_3_out, and_4_out);
  or or_3 (\wait , and_5_out, and_6_out);
  or or_4 (or_4_out, and_7_out, and_8_out);
  and and_9 (win, or_4_out, match);
  and and_10 (lose, or_4_out, not_13_out);
  not not_13 (not_13_out, match);
endmodule
