// Logisim project try_proj1.circ as structural Verilog: 14 circuits, main circuit main
module main (
  input  [3:0] setup_input,
  input  [3:0] game_input,
  input  [3:0] in_3,
  input  [3:0] in_4,
  input  [3:0] in_5,
  input  [3:0] in_6,
  input  [3:0] in_7,
  input  [3:0] in_8,
  input  [2:0] in_9
);

  wire and_2_out, clock, clock_1_out, comparator_1_eq, comparator_2_eq, d_ff_2_q, enter, nand_1_out,
       nor_1_out, nor_2_out, same_digit, state3;
  wire [3:0] Bulls, Bulls_output, Cows, Cows_output, sr1;

  Clock clock_1 (.out(clock_1_out));
  D_Flip_Flop d_ff_1 (.clk(clock_1_out), .D(1'b0), .Q(clock), .preset(enter));  // open: Qn, en, reset
  nor nor_1 (nor_1_out, in_9[0], in_9[1], in_9[2]);
  nor nor_2 (nor_2_out, in_9[2], ~in_9[1], ~in_9[0]);  // NOR_Gate
  Comparator #(.width(4), .mode("unsigned")) comparator_1 (
    .a(Bulls), .b(4'b0100), .eq(comparator_1_eq));  // open: gt, lt
  Comparator #(.width(4), .mode("unsigned")) comparator_2 (
    .a(Cows), .b(4'b0100), .eq(comparator_2_eq));  // open: gt, lt
  and and_1 (state3, nor_2_out, ~same_digit);  // AND_Gate
  nand nand_1 (nand_1_out, comparator_1_eq, comparator_2_eq);
  LED led_1 (.in(same_digit));
  Register #(.width(4)) register_1 (.D(setup_input), .en(nor_1_out), .Q(sr1), .clk(clock));  // open: clr
  Register #(.width(4)) register_2 (.D(in_3), .en(nor_1_out), .Q(sr1), .clk(clock));  // open: clr
  Register #(.width(4)) register_3 (.D(in_5), .en(nor_1_out), .Q(sr1), .clk(clock));  // open: clr
  Register #(.width(4)) register_4 (.D(in_7), .en(nor_1_out), .Q(sr1), .clk(clock));  // open: clr
  D_Flip_Flop d_ff_2 (.clk(clock), .D(state3), .Q(d_ff_2_q));  // open: Qn, preset, en, reset
  Button button_1 (.out(enter));
  assign Bulls_output = and_2_out ? Bulls : 4'bz;  // Controlled_Buffer controlled_buffer_1
  assign Cows_output = and_2_out ? Cows : 4'bz;  // Controlled_Buffer controlled_buffer_2
  and and_2 (and_2_out, nand_1_out, d_ff_2_q);
  Hex_Digit_Display hex_digit_display_1 (.value(Bulls_output));  // open: dp
  Register #(.width(4)) register_5 (.D(game_input), .en(state3), .Q(sr1), .clk(clock));  // open: clr
  Register #(.width(4)) register_6 (.D(in_4), .en(state3), .Q(sr1), .clk(clock));  // open: clr
  Register #(.width(4)) register_7 (.D(in_6), .en(state3), .Q(sr1), .clk(clock));  // open: clr
  Register #(.width(4)) register_8 (.D(in_8), .en(state3), .Q(sr1), .clk(clock));  // open: clr
  Hex_Digit_Display hex_digit_display_2 (.value(Cows_output));  // open: dp
  same_digit same_digit_1 (.t1(game_input), .t2(in_4), .t3(in_6), .t4(in_8), .same_digit(same_digit));  // open: state
  bulls_with_display_toggle_and_samedigit_detector bulls_with_display_toggle_and_samedigit_detector_1 (
    .tr1(sr1), .tr2(sr1), .tr3(sr1), .tr4(sr1), .sr1(sr1), .sr2(sr1), .sr3(sr1), .sr4(sr1), .Bulls(Bulls));  // open: state, match
  cows_with_display_toggle_and_samedigit_detector cows_with_display_toggle_and_samedigit_detector_1 (
    .tr1(sr1), .tr2(sr1), .tr3(sr1), .tr4(sr1), .sr1(sr1), .sr2(sr1), .sr3(sr1), .sr4(sr1), .Cows(Cows));  // open: state

  // Other names for the same wires on the sheet: s1[3:0] = setup_input; s2[3:0] = in_3; s3[3:0] = in_5;
  //   s4[3:0] = in_7; state[2:0] = in_9; t1[3:0] = game_input; t2[3:0] = in_4; t3[3:0] = in_6; t4[3:0] = in_8;
  //   sr2[3:0] = sr1; sr3[3:0] = sr1; sr4[3:0] = sr1; tr1[3:0] = sr1; tr2[3:0] = sr1; tr3[3:0] = sr1; tr4[3:0] = sr1
endmodule

module bulls_with_display_toggle_and_samedigit_detector (
  input  [3:0] tr1,
  input  [3:0] tr2,
  input  [3:0] tr3,
  input  [3:0] tr4,
  input  [3:0] sr1,
  input  [3:0] sr2,
  input  [3:0] sr3,
  input  [3:0] sr4,
  input  [2:0] state,
  output [3:0] Bulls,
  output match
);

  wire and_1_out, and_2_out, and_3_out, comparator_1_eq, comparator_2_eq, comparator_3_eq, comparator_4_eq,
       d_ff_1_q;
  wire [2:0] bitadder_1_out;
  wire [3:0] bit_extender_1_out;

  Comparator #(.width(4)) comparator_1 (.a(sr1), .b(tr1), .eq(comparator_1_eq));  // open: gt, lt
  Comparator #(.width(4)) comparator_2 (.a(sr2), .b(tr2), .eq(comparator_2_eq));  // open: gt, lt
  Comparator #(.width(4)) comparator_3 (.a(sr3), .b(tr3), .eq(comparator_3_eq));  // open: gt, lt
  Comparator #(.width(4)) comparator_4 (.a(sr4), .b(tr4), .eq(comparator_4_eq));  // open: gt, lt
  BitAdder #(.width(1)) bitadder_1 (
    .in0(comparator_1_eq), .in1(comparator_2_eq), .in2(comparator_3_eq), .in3(comparator_4_eq),
    .out(bitadder_1_out));
  assign bit_extender_1_out = {{1{1'b0}}, bitadder_1_out};  // Bit_Extender bit_extender_1
  Comparator #(.width(4)) comparator_5 (.a(bit_extender_1_out), .b(4'b0100), .eq(match));  // open: gt, lt
  assign Bulls = and_1_out ? bit_extender_1_out : 4'bz;  // Controlled_Buffer controlled_buffer_1
  and and_1 (and_1_out, and_3_out, d_ff_1_q);
  D_Flip_Flop d_ff_1 (.Q(d_ff_1_q), .preset(and_2_out));  // open: clk, D, Qn, en, reset
  and and_2 (and_2_out, state[2], ~state[1], ~state[0]);  // AND_Gate
  and and_3 (and_3_out, ~state[2], state[1], state[0]);  // AND_Gate
endmodule

module cows_with_display_toggle_and_samedigit_detector (
  input  [3:0] tr1,
  input  [3:0] tr2,
  input  [3:0] tr3,
  input  [3:0] tr4,
  input  [3:0] sr1,
  input  [3:0] sr2,
  input  [3:0] sr3,
  input  [3:0] sr4,
  input  [2:0] state,
  output [3:0] Cows
);

  wire and_1_out, and_2_out, and_3_out, comparator_1_eq, comparator_2_eq, comparator_3_eq, comparator_4_eq,
       comparator_5_eq, comparator_6_eq, comparator_7_eq, comparator_8_eq, comparator_9_eq, comparator_10_eq,
       comparator_11_eq, comparator_12_eq, d_ff_1_q, or_1_out, or_2_out, or_3_out, or_4_out;
  wire [2:0] bitadder_1_out;
  wire [3:0] bit_extender_1_out;

  Comparator #(.width(4)) comparator_1 (.a(tr1), .b(sr2), .eq(comparator_1_eq));  // open: gt, lt
  Comparator #(.width(4)) comparator_2 (.a(tr2), .b(sr1), .eq(comparator_2_eq));  // open: gt, lt
  Comparator #(.width(4)) comparator_3 (.a(tr3), .b(sr1), .eq(comparator_3_eq));  // open: gt, lt
  Comparator #(.width(4)) comparator_4 (.a(tr4), .b(sr1), .eq(comparator_4_eq));  // open: gt, lt
  Comparator #(.width(4)) comparator_5 (.a(tr1), .b(sr3), .eq(comparator_5_eq));  // open: gt, lt
  Comparator #(.width(4)) comparator_6 (.a(tr2), .b(sr3), .eq(comparator_6_eq));  // open: gt, lt
  Comparator #(.width(4)) comparator_7 (.a(tr3), .b(sr2), .eq(comparator_7_eq));  // open: gt, lt
  Comparator #(.width(4)) comparator_8 (.a(tr4), .b(sr2), .eq(comparator_8_eq));  // open: gt, lt
  Comparator #(.width(4)) comparator_9 (.a(tr4), .b(sr3), .eq(comparator_9_eq));  // open: gt, lt
  Comparator #(.width(4)) comparator_10 (.a(tr1), .b(sr4), .eq(comparator_10_eq));  // open: gt, lt
  Comparator #(.width(4)) comparator_11 (.a(tr2), .b(sr4), .eq(comparator_11_eq));  // open: gt, lt
  Comparator #(.width(4)) comparator_12 (.a(tr3), .b(sr4), .eq(comparator_12_eq));  // open: gt, lt
  or or_1 (or_1_out, comparator_4_eq, comparator_8_eq, comparator_9_eq);
  or or_2 (or_2_out, comparator_1_eq, comparator_5_eq, comparator_10_eq);
  or or_3 (or_3_out, comparator_2_eq, comparator_6_eq, comparator_11_eq);
  or or_4 (or_4_out, comparator_3_eq, comparator_7_eq, comparator_12_eq);
  BitAdder #(.width(1)) bitadder_1 (
    .in0(or_2_out), .in1(or_3_out), .in2(or_4_out), .in3(or_1_out), .out(bitadder_1_out));
  assign bit_extender_1_out = {{1{1'b0}}, bitadder_1_out};  // Bit_Extender bit_extender_1
  assign Cows = and_1_out ? bit_extender_1_out : 4'bz;  // Controlled_Buffer controlled_buffer_1
  and and_1 (and_1_out, and_3_out, d_ff_1_q);
  D_Flip_Flop d_ff_1 (.Q(d_ff_1_q), .preset(and_2_out));  // open: clk, D, Qn, en, reset
  and and_2 (and_2_out, state[2], ~state[1], ~state[0]);  // AND_Gate
  and and_3 (and_3_out, ~state[2], state[1], state[0]);  // AND_Gate
endmodule

module same_digit (
  input  [3:0] t1,
  input  [3:0] t2,
  input  [3:0] t3,
  input  [3:0] t4,
  input  [2:0] state,
  output same_digit
);

  wire and_1_out, and_2_out, comparator_1_eq, comparator_2_eq, comparator_3_eq, comparator_4_eq,
       comparator_5_eq, comparator_6_eq, comparator_7_eq, comparator_8_eq, comparator_9_eq, comparator_10_eq,
       comparator_11_eq, comparator_12_eq, or_1_out, or_2_out;

  Comparator #(.width(4)) comparator_1 (.a(t1), .b(t2), .eq(comparator_1_eq));  // open: gt, lt
  Comparator #(.width(4)) comparator_2 (.a(t2), .b(t1), .eq(comparator_2_eq));  // open: gt, lt
  Comparator #(.width(4)) comparator_3 (.a(t3), .b(t1), .eq(comparator_3_eq));  // open: gt, lt
  Comparator #(.width(4)) comparator_4 (.a(t4), .b(t1), .eq(comparator_4_eq));  // open: gt, lt
  Comparator #(.width(4)) comparator_5 (.a(t1), .b(t3), .eq(comparator_5_eq));  // open: gt, lt
  Comparator #(.width(4)) comparator_6 (.a(t2), .b(t3), .eq(comparator_6_eq));  // open: gt, lt
  Comparator #(.width(4)) comparator_7 (.a(t3), .b(t2), .eq(comparator_7_eq));  // open: gt, lt
  Comparator #(.width(4)) comparator_8 (.a(t4), .b(t2), .eq(comparator_8_eq));  // open: gt, lt
  Comparator #(.width(4)) comparator_9 (.a(t1), .b(t4), .eq(comparator_9_eq));  // open: gt, lt
  Comparator #(.width(4)) comparator_10 (.a(t2), .b(t4), .eq(comparator_10_eq));  // open: gt, lt
  Comparator #(.width(4)) comparator_11 (.a(t3), .b(t4), .eq(comparator_11_eq));  // open: gt, lt
  Comparator #(.width(4)) comparator_12 (.a(t4), .b(t3), .eq(comparator_12_eq));  // open: gt, lt
  or or_1 (or_1_out, comparator_1_eq, comparator_5_eq, comparator_9_eq, comparator_2_eq, comparator_6_eq, comparator_10_eq, comparator_3_eq, comparator_7_eq, comparator_11_eq, comparator_4_eq, comparator_8_eq, comparator_12_eq);
  assign same_digit = or_2_out ? or_1_out : 1'bz;  // Controlled_Buffer controlled_buffer_1
  or or_2 (or_2_out, and_1_out, and_2_out);
  and and_1 (and_1_out, ~state[2], ~state[1], ~state[0]);  // AND_Gate
  and and_2 (and_2_out, ~state[2], state[1], state[0]);  // AND_Gate
endmodule

module store_memory_with_samedigit__detector (
  input  [3:0] I0,
  input  [3:0] I1,
  input  [3:0] I2,
  input  [3:0] I3,
  input  Enter,
  input  clock,
  input  Error,
  input  [2:0] state,
  output [3:0] s0,
  output [3:0] s1,
  output [3:0] s2,
  output [3:0] s3
);

  wire and_1_out, and_2_out;

  and and_1 (and_1_out, Enter, ~Error);  // AND_Gate
  and and_2 (and_2_out, and_1_out, ~state[2], ~state[1], ~state[0]);  // AND_Gate
  Register #(.width(4)) register_1 (.D(I0), .en(and_2_out), .Q(s0), .clk(clock));  // open: clr
  Register #(.width(4)) register_2 (.D(I1), .en(and_2_out), .Q(s1), .clk(clock));  // open: clr
  Register #(.width(4)) register_3 (.D(I2), .en(and_2_out), .Q(s2), .clk(clock));  // open: clr
  Register #(.width(4)) register_4 (.D(I3), .en(and_2_out), .Q(s3), .clk(clock));  // open: clr
endmodule

module win_lives_memory_with_samedigit_detector (
  input  match,
  input  error,
  input  clock,
  input  [2:0] state,
  output [3:0] wins,
  output [2:0] lives
);

  wire and_1_out, and_2_out, and_3_out, and_4_out;
  wire [2:0] subtractor_1_out;
  wire [3:0] adder_1_out;

  and and_1 (and_1_out, match, ~error);  // AND_Gate
  Adder #(.width(4)) adder_1 (.a(wins), .b(4'b0001), .out(adder_1_out));  // open: cin, cout
  Subtractor #(.width(3)) subtractor_1 (.a(lives), .b(3'b001), .out(subtractor_1_out));  // open: bin, bout
  and and_2 (and_2_out, and_1_out, and_3_out);
  and and_3 (and_3_out, ~state[0], ~state[1], state[2]);  // AND_Gate
  Register #(.width(4)) u_wins (.D(adder_1_out), .en(and_2_out), .Q(wins), .clk(clock));  // open: clr
  and and_4 (and_4_out, ~state[0], ~state[1], ~state[2]);  // AND_Gate
  D_Flip_Flop d_ff_1 (
    .clk(clock), .D(subtractor_1_out[0]), .Q(lives[0]), .preset(and_4_out), .en(and_3_out));  // open: Qn, reset
  D_Flip_Flop d_ff_2 (
    .clk(clock), .D(subtractor_1_out[1]), .Q(lives[1]), .preset(and_4_out), .en(and_3_out));  // open: Qn, reset
  D_Flip_Flop d_ff_3 (
    .clk(clock), .D(subtractor_1_out[2]), .Q(lives[2]), .preset(and_4_out), .en(and_3_out));  // open: Qn, reset
endmodule

module store_memory_with_samedigit_detector_trystage (
  input  [3:0] I0,
  input  [3:0] I1,
  input  [3:0] I2,
  input  [3:0] I3,
  input  Enter,
  input  clock,
  input  Error,
  input  [2:0] state,
  output [3:0] s0,
  output [3:0] s1,
  output [3:0] s2,
  output [3:0] s3
);

  wire and_1_out, and_2_out;

  and and_1 (and_1_out, Enter, ~Error);  // AND_Gate
  and and_2 (and_2_out, and_1_out, ~state[2], state[1], state[0]);  // AND_Gate
  Register #(.width(4)) register_1 (.D(I0), .en(and_2_out), .Q(s0), .clk(clock));  // open: clr
  Register #(.width(4)) register_2 (.D(I1), .en(and_2_out), .Q(s1), .clk(clock));  // open: clr
  Register #(.width(4)) register_3 (.D(I2), .en(and_2_out), .Q(s2), .clk(clock));  // open: clr
  Register #(.width(4)) register_4 (.D(I3), .en(and_2_out), .Q(s3), .clk(clock));  // open: clr
endmodule

module Random_generator (
  input  random_button,
  input  [2:0] state,
  input  clock,
  output [15:0] Rand_output
);

  wire and_1_out, comparator_1_gt, comparator_2_gt, comparator_3_gt, comparator_4_gt;
  wire [3:0] multiplexer_4_out, subtractor_1_out, subtractor_2_out, subtractor_3_out, subtractor_4_out;
  wire [11:0] multiplexer_1_out;
  wire [15:0] random_1_out, register_1_q;

  Random #(.width(16), .seed(21140145)) random_1 (.clk(clock), .next(random_button), .out(random_1_out));  // open: clr
  Comparator #(.width(4), .mode("unsigned")) comparator_1 (
    .a(random_1_out[3:0]), .b(4'b1001), .gt(comparator_1_gt));  // open: eq, lt
  Comparator #(.width(4), .mode("unsigned")) comparator_2 (
    .a(random_1_out[7:4]), .b(4'b1001), .gt(comparator_2_gt));  // open: eq, lt
  Comparator #(.width(4), .mode("unsigned")) comparator_3 (
    .a(random_1_out[11:8]), .b(4'b1001), .gt(comparator_3_gt));  // open: eq, lt
  Comparator #(.width(4), .mode("unsigned")) comparator_4 (
    .a(random_1_out[15:12]), .b(4'b1001), .gt(comparator_4_gt));  // open: eq, lt
  Subtractor #(.width(4)) subtractor_1 (.a(random_1_out[3:0]), .b(4'b1010), .out(subtractor_1_out));  // open: bin, bout
  Multiplexer #(.width(4)) multiplexer_1 (
    .in0(random_1_out[3:0]), .in1(subtractor_1_out), .out(multiplexer_1_out[3:0]), .sel(comparator_1_gt));  // open: en
  Multiplexer #(.width(4)) multiplexer_2 (
    .in0(random_1_out[7:4]), .in1(subtractor_2_out), .out(multiplexer_1_out[7:4]), .sel(comparator_2_gt));  // open: en
  Subtractor #(.width(4)) subtractor_2 (.a(random_1_out[7:4]), .b(4'b1010), .out(subtractor_2_out));  // open: bin, bout
  Multiplexer #(.width(4)) multiplexer_3 (
    .in0(random_1_out[11:8]), .in1(subtractor_3_out), .out(multiplexer_1_out[11:8]), .sel(comparator_3_gt));  // open: en
  Subtractor #(.width(4)) subtractor_3 (
    .a(random_1_out[11:8]), .b(4'b1010), .out(subtractor_3_out));  // open: bin, bout
  Subtractor #(.width(4)) subtractor_4 (
    .a(random_1_out[15:12]), .b(4'b1010), .out(subtractor_4_out));  // open: bin, bout
  Multiplexer #(.width(4)) multiplexer_4 (
    .in0(random_1_out[15:12]), .in1(subtractor_4_out), .out(multiplexer_4_out), .sel(comparator_4_gt));  // open: en
  Hex_Digit_Display hex_digit_display_1 (.value(multiplexer_1_out[3:0]));  // open: dp
  Hex_Digit_Display hex_digit_display_2 (.value(multiplexer_1_out[11:8]));  // open: dp
  Hex_Digit_Display hex_digit_display_3 (.value(multiplexer_1_out[7:4]));  // open: dp
  Register #(.width(16)) register_1 (
    .D({multiplexer_4_out, multiplexer_1_out}), .Q(register_1_q), .clk(clock));  // open: en, clr
  Hex_Digit_Display hex_digit_display_4 (.value(multiplexer_4_out));  // open: dp
  assign Rand_output = and_1_out ? register_1_q : 16'bz;  // Controlled_Buffer controlled_buffer_1
  and and_1 (and_1_out, ~state[2], ~state[1], ~state[0]);  // AND_Gate
endmodule

module Digit_input_with_random_input (
  input  _0,
  input  _1,
  input  _2,
  input  _3,
  input  _4,
  input  _5,
  input  _6,
  input  _7,
  input  _8,
  input  _9,
  input  [15:0] random_input,
  input  random_click,
  input  clock,
  input  [1:0] in_14,
  input  [2:0] State,
  output [3:0] I0,
  output [3:0] I1,
  output [3:0] I2,
  output [3:0] I3
);

  wire and_1_out, and_2_out, and_3_out, and_4_out, and_5_out, and_6_out, and_7_out, and_8_out, and_9_out,
       decoder_1_out0, decoder_1_out1, decoder_1_out2, decoder_1_out3, or_1_out, or_2_out, or_3_out,
       or_4_out, or_5_out, or_6_out, priority_encoder_1_gs;
  wire [3:0] multiplexer_1_out, multiplexer_2_out, multiplexer_3_out, multiplexer_4_out,
       priority_encoder_1_out;

  Priority_Encoder #(.select(4)) priority_encoder_1 (
    .in0(_0), .in1(_1), .in2(_2), .in3(_3), .in4(_4), .in5(_5), .in6(_6), .in7(_7), .in8(_8), .in9(_9),
    .out(priority_encoder_1_out), .gs(priority_encoder_1_gs));  // open: in10, in11, in12, in13, in14, in15, en_out, en_in
  // Probe on priority_encoder_1_out
  Multiplexer #(.width(4)) multiplexer_1 (
    .in0(priority_encoder_1_out), .in1(random_input[3:0]), .out(multiplexer_1_out), .sel(random_click));  // open: en
  or or_1 (or_1_out, random_click, and_3_out);
  Multiplexer #(.width(4)) multiplexer_2 (
    .in0(priority_encoder_1_out), .in1(random_input[7:4]), .out(multiplexer_2_out), .sel(random_click));  // open: en
  or or_2 (or_2_out, random_click, and_4_out);
  Multiplexer #(.width(4)) multiplexer_3 (
    .in0(priority_encoder_1_out), .in1(random_input[11:8]), .out(multiplexer_3_out), .sel(random_click));  // open: en
  or or_3 (or_3_out, random_click, and_5_out);
  Multiplexer #(.width(4)) multiplexer_4 (
    .in0(priority_encoder_1_out), .in1(random_input[15:12]), .out(multiplexer_4_out), .sel(random_click));  // open: en
  or or_4 (or_4_out, random_click, and_6_out);
  Decoder #(.select(2)) decoder_1 (
    .out0(decoder_1_out0), .out1(decoder_1_out1), .out2(decoder_1_out2), .out3(decoder_1_out3), .sel(in_14));  // open: en
  Register #(.width(4)) register_1 (.D(multiplexer_1_out), .en(or_1_out), .Q(I0), .clk(clock), .clr(or_5_out));
  Register #(.width(4)) register_2 (.D(multiplexer_2_out), .en(or_2_out), .Q(I1), .clk(clock), .clr(or_5_out));
  Register #(.width(4)) register_3 (.D(multiplexer_3_out), .en(or_3_out), .Q(I2), .clk(clock), .clr(or_5_out));
  Register #(.width(4)) register_4 (.D(multiplexer_4_out), .en(or_4_out), .Q(I3), .clk(clock), .clr(or_5_out));
  or or_5 (or_5_out, and_1_out, and_7_out);
  and and_1 (and_1_out, State[2], State[1], State[0]);
  and and_2 (and_2_out, or_6_out, priority_encoder_1_gs);
  and and_3 (and_3_out, and_2_out, decoder_1_out0);
  and and_4 (and_4_out, and_2_out, decoder_1_out1);
  and and_5 (and_5_out, and_2_out, decoder_1_out2);
  and and_6 (and_6_out, and_2_out, decoder_1_out3);
  and and_7 (and_7_out, ~State[2], State[1], ~State[0]);  // AND_Gate
  or or_6 (or_6_out, and_8_out, and_9_out);
  and and_8 (and_8_out, ~State[2], ~State[1], ~State[0]);  // AND_Gate
  and and_9 (and_9_out, ~State[2], State[1], State[0]);  // AND_Gate

  // Other names for the same wires on the sheet: Clock_T = clock
endmodule

module _7_seg_decoder (
  input  [3:0] \input ,
  output a,
  output b,
  output c,
  output d,
  output e,
  output f,
  output g
);

  wire nand_1_out, nand_2_out, nand_3_out, nand_4_out, nand_5_out, nand_6_out, nand_7_out, nand_8_out,
       nand_9_out, nand_10_out, nand_11_out, nand_12_out, nand_13_out, nand_14_out, nand_15_out, nand_16_out,
       nand_17_out, nand_18_out, nand_19_out, nand_20_out, nand_21_out, nand_22_out, nand_23_out,
       nand_24_out, nand_25_out, nand_26_out, nand_27_out, nand_28_out, nand_29_out, nand_30_out,
       nand_31_out, nand_32_out, nand_33_out, nand_34_out, nand_35_out, nand_36_out, nand_37_out,
       nand_38_out, nand_39_out, nand_40_out, nand_41_out, nand_42_out, nand_43_out, nand_44_out,
       nand_45_out, nand_46_out, nand_47_out, nand_48_out, nand_49_out, nand_50_out, nand_51_out,
       nand_52_out, nand_53_out, nand_54_out, nand_55_out, nand_56_out, nand_57_out, nand_58_out,
       nand_59_out, nand_60_out, nand_61_out, nand_62_out, nand_63_out, nand_64_out, nand_65_out,
       nand_66_out, nand_67_out, nand_68_out, nand_69_out, nand_70_out, nand_71_out, nand_72_out,
       nand_73_out, nand_74_out, nand_75_out, nand_76_out, nand_77_out, nand_78_out, nand_79_out,
       nand_80_out, nand_81_out, nand_82_out, nand_83_out, nand_84_out, nand_85_out, nand_86_out,
       nand_87_out, nand_88_out, nand_89_out, nand_90_out, nand_91_out, nand_92_out, nand_93_out,
       nand_94_out, nand_95_out, nand_96_out, nand_97_out, nand_98_out, nand_99_out, nand_100_out,
       nand_101_out, nand_102_out, nand_103_out, nand_104_out, nand_106_out, nand_107_out, nand_108_out,
       nand_109_out, nand_110_out, nand_111_out, nand_112_out, nand_113_out, nand_114_out, nand_115_out,
       nand_116_out, nand_117_out, nand_118_out, nand_119_out, nand_120_out, nand_121_out, nand_122_out,
       nand_123_out, nand_124_out, nand_125_out, nand_126_out, nand_127_out, nand_128_out, nand_129_out,
       nand_130_out, nand_131_out, nand_132_out, nand_133_out, nand_134_out, nand_136_out, nand_137_out,
       nand_138_out, nand_139_out, nand_141_out, nand_142_out, nand_143_out, nand_144_out, nand_145_out,
       nand_146_out, nand_147_out, nand_148_out;

  nand nand_1 (nand_1_out, \input [2], \input [2]);
  nand nand_2 (nand_2_out, \input [3], \input [3]);
  nand nand_3 (nand_3_out, \input [1], \input [1]);
  nand nand_4 (nand_4_out, \input [3], \input [3]);
  nand nand_5 (nand_5_out, \input [1], \input [1]);
  nand nand_6 (nand_6_out, \input [3], \input [3]);
  nand nand_7 (nand_7_out, \input [3], \input [3]);
  nand nand_8 (nand_8_out, \input [2], \input [2]);
  nand nand_9 (nand_9_out, \input [2], \input [2]);
  nand nand_10 (nand_10_out, \input [2], \input [2]);
  nand nand_11 (nand_11_out, \input [0], \input [0]);
  nand nand_12 (nand_12_out, \input [0], \input [0]);
  nand nand_13 (nand_13_out, \input [3], \input [3]);
  nand nand_14 (nand_14_out, \input [2], \input [2]);
  nand nand_15 (nand_15_out, \input [0], \input [0]);
  nand nand_16 (nand_16_out, \input [3], \input [3]);
  nand nand_17 (nand_17_out, \input [3], nand_1_out);
  nand nand_18 (nand_18_out, nand_2_out, nand_3_out);
  nand nand_19 (nand_19_out, nand_4_out, nand_5_out);
  nand nand_20 (nand_20_out, nand_6_out, \input [0]);
  nand nand_21 (nand_21_out, nand_7_out, nand_8_out);
  nand nand_22 (nand_22_out, nand_9_out, \input [1]);
  nand nand_23 (nand_23_out, nand_10_out, nand_11_out);
  nand nand_24 (nand_24_out, \input [1], nand_12_out);
  nand nand_25 (nand_25_out, \input [3], \input [1]);
  nand nand_26 (nand_26_out, \input [3], \input [2]);
  nand nand_27 (nand_27_out, nand_13_out, \input [2]);
  nand nand_28 (nand_28_out, nand_14_out, \input [1]);
  nand nand_29 (nand_29_out, \input [1], nand_15_out);
  nand nand_30 (nand_30_out, nand_16_out, \input [2]);
  nand nand_31 (nand_31_out, \input [2], \input [2]);
  nand nand_32 (nand_32_out, \input [0], \input [0]);
  nand nand_33 (nand_33_out, \input [3], \input [3]);
  nand nand_34 (nand_34_out, \input [3], \input [3]);
  nand nand_35 (nand_35_out, nand_17_out, nand_17_out);
  nand nand_36 (nand_36_out, \input [1], \input [1]);
  nand nand_37 (nand_37_out, \input [3], \input [3]);
  nand nand_38 (nand_38_out, \input [2], \input [2]);
  nand nand_39 (nand_39_out, nand_18_out, nand_18_out);
  nand nand_40 (nand_40_out, \input [0], \input [0]);
  nand nand_41 (nand_41_out, \input [3], \input [3]);
  nand nand_42 (nand_42_out, \input [1], \input [1]);
  nand nand_43 (nand_43_out, nand_19_out, nand_20_out);
  nand nand_44 (nand_44_out, \input [1], \input [1]);
  nand nand_45 (nand_45_out, \input [3], \input [3]);
  nand nand_46 (nand_46_out, \input [2], \input [2]);
  nand nand_47 (nand_47_out, nand_21_out, nand_21_out);
  nand nand_48 (nand_48_out, \input [0], \input [0]);
  nand nand_49 (nand_49_out, nand_22_out, nand_22_out);
  nand nand_50 (nand_50_out, \input [1], \input [1]);
  nand nand_51 (nand_51_out, \input [1], \input [1]);
  nand nand_52 (nand_52_out, nand_23_out, nand_24_out);
  nand nand_53 (nand_53_out, nand_25_out, nand_26_out);
  nand nand_54 (nand_54_out, \input [1], \input [1]);
  nand nand_55 (nand_55_out, \input [0], \input [0]);
  nand nand_56 (nand_56_out, nand_27_out, nand_27_out);
  nand nand_57 (nand_57_out, \input [1], \input [1]);
  nand nand_58 (nand_58_out, nand_28_out, nand_29_out);
  nand nand_59 (nand_59_out, nand_30_out, nand_30_out);
  nand nand_60 (nand_60_out, \input [1], \input [1]);
  nand nand_61 (nand_61_out, \input [2], \input [2]);
  nand nand_62 (nand_62_out, nand_31_out, nand_32_out);
  nand nand_63 (nand_63_out, nand_33_out, \input [1]);
  nand nand_64 (nand_64_out, nand_34_out, \input [2]);
  nand nand_65 (nand_65_out, \input [2], \input [1]);
  nand nand_66 (nand_66_out, nand_35_out, nand_36_out);
  nand nand_67 (nand_67_out, nand_37_out, nand_38_out);
  nand nand_68 (nand_68_out, nand_39_out, nand_40_out);
  nand nand_69 (nand_69_out, nand_41_out, \input [1]);
  nand nand_70 (nand_70_out, \input [3], nand_42_out);
  nand nand_71 (nand_71_out, nand_43_out, nand_43_out);
  nand nand_72 (nand_72_out, nand_44_out, \input [0]);
  nand nand_73 (nand_73_out, nand_45_out, \input [2]);
  nand nand_74 (nand_74_out, \input [3], nand_46_out);
  nand nand_75 (nand_75_out, nand_47_out, nand_48_out);
  nand nand_76 (nand_76_out, nand_49_out, \input [0]);
  nand nand_77 (nand_77_out, \input [2], nand_50_out);
  nand nand_78 (nand_78_out, \input [2], \input [1]);
  nand nand_79 (nand_79_out, \input [3], nand_51_out);
  nand nand_80 (nand_80_out, nand_52_out, nand_52_out);
  nand nand_81 (nand_81_out, nand_53_out, nand_53_out);
  nand nand_82 (nand_82_out, nand_54_out, nand_55_out);
  nand nand_83 (nand_83_out, nand_56_out, nand_57_out);
  nand nand_84 (nand_84_out, nand_58_out, nand_58_out);
  nand nand_85 (nand_85_out, nand_59_out, nand_60_out);
  nand nand_86 (nand_86_out, \input [3], nand_61_out);
  nand nand_87 (nand_87_out, \input [3], \input [0]);
  nand nand_88 (nand_88_out, nand_62_out, nand_63_out);
  nand nand_89 (nand_89_out, nand_64_out, nand_64_out);
  nand nand_90 (nand_90_out, nand_65_out, nand_66_out);
  nand nand_91 (nand_91_out, \input [0], \input [0]);
  nand nand_92 (nand_92_out, nand_67_out, nand_68_out);
  nand nand_93 (nand_93_out, \input [2], \input [2]);
  nand nand_94 (nand_94_out, \input [0], \input [0]);
  nand nand_95 (nand_95_out, nand_69_out, nand_69_out);
  nand nand_96 (nand_96_out, nand_70_out, nand_70_out);
  nand nand_97 (nand_97_out, nand_71_out, nand_72_out);
  nand nand_98 (nand_98_out, nand_73_out, nand_74_out);
  nand nand_99 (nand_99_out, nand_75_out, nand_76_out);
  nand nand_100 (nand_100_out, nand_77_out, nand_77_out);
  nand nand_101 (nand_101_out, nand_78_out, nand_78_out);
  nand nand_102 (nand_102_out, \input [0], \input [0]);
  nand nand_103 (nand_103_out, nand_79_out, nand_79_out);
  nand nand_104 (nand_104_out, \input [0], \input [0]);
  nand nand_105 (e, nand_80_out, nand_81_out);
  nand nand_106 (nand_106_out, nand_82_out, nand_83_out);
  nand nand_107 (nand_107_out, \input [0], \input [0]);
  nand nand_108 (nand_108_out, \input [2], \input [2]);
  nand nand_109 (nand_109_out, nand_84_out, nand_85_out);
  nand nand_110 (nand_110_out, nand_86_out, nand_87_out);
  nand nand_111 (nand_111_out, nand_88_out, nand_88_out);
  nand nand_112 (nand_112_out, nand_89_out, \input [0]);
  nand nand_113 (nand_113_out, nand_90_out, nand_90_out);
  nand nand_114 (nand_114_out, \input [3], nand_91_out);
  nand nand_115 (nand_115_out, nand_92_out, nand_92_out);
  nand nand_116 (nand_116_out, nand_93_out, nand_94_out);
  nand nand_117 (nand_117_out, nand_95_out, \input [0]);
  nand nand_118 (nand_118_out, nand_96_out, \input [0]);
  nand nand_119 (nand_119_out, nand_97_out, nand_97_out);
  nand nand_120 (nand_120_out, nand_98_out, nand_98_out);
  nand nand_121 (nand_121_out, nand_99_out, nand_99_out);
  nand nand_122 (nand_122_out, nand_100_out, \input [0]);
  nand nand_123 (nand_123_out, nand_101_out, nand_102_out);
  nand nand_124 (nand_124_out, nand_103_out, nand_104_out);
  nand nand_125 (nand_125_out, nand_106_out, nand_106_out);
  nand nand_126 (nand_126_out, \input [2], nand_107_out);
  nand nand_127 (nand_127_out, \input [3], nand_108_out);
  nand nand_128 (nand_128_out, \input [3], \input [1]);
  nand nand_129 (nand_129_out, nand_109_out, nand_109_out);
  nand nand_130 (nand_130_out, nand_110_out, nand_110_out);
  nand nand_131 (nand_131_out, nand_111_out, nand_112_out);
  nand nand_132 (nand_132_out, nand_113_out, nand_114_out);
  nand nand_133 (nand_133_out, nand_115_out, nand_116_out);
  nand nand_134 (nand_134_out, nand_117_out, nand_118_out);
  nand nand_135 (c, nand_119_out, nand_120_out);
  nand nand_136 (nand_136_out, nand_121_out, nand_122_out);
  nand nand_137 (nand_137_out, nand_123_out, nand_124_out);
  nand nand_138 (nand_138_out, nand_125_out, nand_126_out);
  nand nand_139 (nand_139_out, nand_127_out, nand_128_out);
  nand nand_140 (g, nand_129_out, nand_130_out);
  nand nand_141 (nand_141_out, nand_131_out, nand_131_out);
  nand nand_142 (nand_142_out, nand_132_out, nand_132_out);
  nand nand_143 (nand_143_out, nand_133_out, nand_133_out);
  nand nand_144 (nand_144_out, nand_134_out, nand_134_out);
  nand nand_145 (nand_145_out, nand_136_out, nand_136_out);
  nand nand_146 (nand_146_out, nand_137_out, nand_137_out);
  nand nand_147 (nand_147_out, nand_138_out, nand_138_out);
  nand nand_148 (nand_148_out, nand_139_out, nand_139_out);
  nand nand_149 (a, nand_141_out, nand_142_out);
  nand nand_150 (b, nand_143_out, nand_144_out);
  nand nand_151 (d, nand_145_out, nand_146_out);
  nand nand_152 (f, nand_147_out, nand_148_out);
endmodule

module bulls_cows_error_display (
  input  [3:0] t1,
  input  [3:0] t2,
  input  [3:0] t3,
  input  [3:0] t4,
  input  [3:0] tr1,
  input  [3:0] tr2,
  input  [3:0] tr3,
  input  [3:0] tr4,
  input  [3:0] sr1,
  input  [3:0] sr2,
  input  [3:0] sr3,
  input  [3:0] sr4,
  input  [2:0] state,
  output [3:0] D0,
  output [3:0] D1,
  output [3:0] D2,
  output [3:0] D3,
  output same_digit,
  output match,
  output [3:0] Bulls,
  output [3:0] Cows
);

  wire and_1_out, and_2_out, and_3_out, and_4_out, and_5_out, and_6_out, and_7_out, comparator_1_eq,
       comparator_2_eq, comparator_3_eq, comparator_4_eq, comparator_5_eq, comparator_6_eq, comparator_7_eq,
       comparator_8_eq, comparator_9_eq, comparator_10_eq, comparator_11_eq, comparator_12_eq,
       comparator_13_eq, comparator_14_eq, comparator_15_eq, comparator_16_eq, comparator_17_eq,
       comparator_18_eq, comparator_19_eq, comparator_20_eq, comparator_21_eq, comparator_22_eq,
       comparator_23_eq, comparator_24_eq, comparator_25_eq, comparator_26_eq, comparator_27_eq,
       comparator_28_eq, d_ff_1_q, or_1_out, or_2_out, or_3_out, or_4_out, or_5_out, or_6_out, or_7_out,
       xnor_1_out;
  wire [2:0] bitadder_1_out, bitadder_2_out;
  wire [3:0] bit_extender_1_out, bit_extender_2_out;

  Comparator #(.width(4)) comparator_1 (.a(t1), .b(t2), .eq(comparator_1_eq));  // open: gt, lt
  Comparator #(.width(4)) comparator_2 (.a(t2), .b(t1), .eq(comparator_2_eq));  // open: gt, lt
  Comparator #(.width(4)) comparator_3 (.a(t3), .b(t1), .eq(comparator_3_eq));  // open: gt, lt
  Comparator #(.width(4)) comparator_4 (.a(t4), .b(t1), .eq(comparator_4_eq));  // open: gt, lt
  Multiplexer #(.width(16)) multiplexer_1 (
    .in0({t4, t3, t2, t1}), .in1({sr4, sr3, sr2, sr1}), .out({D3, D2, D1, D0}), .sel(or_7_out),
    .en(xnor_1_out));
  Comparator #(.width(4)) comparator_5 (.a(tr1), .b(sr2), .eq(comparator_5_eq));  // open: gt, lt
  Comparator #(.width(4)) comparator_6 (.a(tr2), .b(sr1), .eq(comparator_6_eq));  // open: gt, lt
  Comparator #(.width(4)) comparator_7 (.a(tr3), .b(sr1), .eq(comparator_7_eq));  // open: gt, lt
  Comparator #(.width(4)) comparator_8 (.a(tr4), .b(sr1), .eq(comparator_8_eq));  // open: gt, lt
  Comparator #(.width(4)) comparator_9 (.a(t1), .b(t3), .eq(comparator_9_eq));  // open: gt, lt
  Comparator #(.width(4)) comparator_10 (.a(t2), .b(t3), .eq(comparator_10_eq));  // open: gt, lt
  Comparator #(.width(4)) comparator_11 (.a(t3), .b(t2), .eq(comparator_11_eq));  // open: gt, lt
  Comparator #(.width(4)) comparator_12 (.a(t4), .b(t2), .eq(comparator_12_eq));  // open: gt, lt
  // Probe on {D3, D2, D1, D0}
  Comparator #(.width(4)) comparator_13 (.a(sr1), .b(tr1), .eq(comparator_13_eq));  // open: gt, lt
  Comparator #(.width(4)) comparator_14 (.a(sr2), .b(tr2), .eq(comparator_14_eq));  // open: gt, lt
  Comparator #(.width(4)) comparator_15 (.a(sr3), .b(tr3), .eq(comparator_15_eq));  // open: gt, lt
  Comparator #(.width(4)) comparator_16 (.a(sr4), .b(tr4), .eq(comparator_16_eq));  // open: gt, lt
  Comparator #(.width(4)) comparator_17 (.a(tr1), .b(sr3), .eq(comparator_17_eq));  // open: gt, lt
  Comparator #(.width(4)) comparator_18 (.a(tr2), .b(sr3), .eq(comparator_18_eq));  // open: gt, lt
  Comparator #(.width(4)) comparator_19 (.a(tr3), .b(sr2), .eq(comparator_19_eq));  // open: gt, lt
  Comparator #(.width(4)) comparator_20 (.a(tr4), .b(sr2), .eq(comparator_20_eq));  // open: gt, lt
  Comparator #(.width(4)) comparator_21 (.a(tr4), .b(sr3), .eq(comparator_21_eq));  // open: gt, lt
  Comparator #(.width(4)) comparator_22 (.a(t1), .b(t4), .eq(comparator_22_eq));  // open: gt, lt
  Comparator #(.width(4)) comparator_23 (.a(t2), .b(t4), .eq(comparator_23_eq));  // open: gt, lt
  Comparator #(.width(4)) comparator_24 (.a(t3), .b(t4), .eq(comparator_24_eq));  // open: gt, lt
  Comparator #(.width(4)) comparator_25 (.a(t4), .b(t3), .eq(comparator_25_eq));  // open: gt, lt
  BitAdder #(.width(1)) bitadder_1 (
    .in0(comparator_13_eq), .in1(comparator_14_eq), .in2(comparator_15_eq), .in3(comparator_16_eq),
    .out(bitadder_1_out));
  Comparator #(.width(4)) comparator_26 (.a(tr1), .b(sr4), .eq(comparator_26_eq));  // open: gt, lt
  Comparator #(.width(4)) comparator_27 (.a(tr2), .b(sr4), .eq(comparator_27_eq));  // open: gt, lt
  Comparator #(.width(4)) comparator_28 (.a(tr3), .b(sr4), .eq(comparator_28_eq));  // open: gt, lt
  or or_1 (or_1_out, comparator_8_eq, comparator_20_eq, comparator_21_eq);
  assign bit_extender_1_out = {{1{1'b0}}, bitadder_1_out};  // Bit_Extender bit_extender_1
  or or_2 (or_2_out, comparator_5_eq, comparator_17_eq, comparator_26_eq);
  or or_3 (or_3_out, comparator_6_eq, comparator_18_eq, comparator_27_eq);
  or or_4 (or_4_out, comparator_7_eq, comparator_19_eq, comparator_28_eq);
  or or_5 (or_5_out, comparator_1_eq, comparator_9_eq, comparator_22_eq, comparator_2_eq, comparator_10_eq, comparator_23_eq, comparator_3_eq, comparator_11_eq, comparator_24_eq, comparator_4_eq, comparator_12_eq, comparator_25_eq);
  assign bit_extender_2_out = {{1{1'b0}}, bitadder_2_out};  // Bit_Extender bit_extender_2
  BitAdder #(.width(1)) bitadder_2 (
    .in0(or_2_out), .in1(or_3_out), .in2(or_4_out), .in3(or_1_out), .out(bitadder_2_out));
  assign same_digit = or_6_out ? or_5_out : 1'bz;  // Controlled_Buffer controlled_buffer_1
  assign Bulls = and_1_out ? bit_extender_1_out : 4'bz;  // Controlled_Buffer controlled_buffer_2
  assign Cows = and_1_out ? bit_extender_2_out : 4'bz;  // Controlled_Buffer controlled_buffer_3
  and and_1 (and_1_out, and_2_out, d_ff_1_q);
  D_Flip_Flop d_ff_1 (.Q(d_ff_1_q), .preset(and_3_out), .reset(and_4_out));  // open: clk, D, Qn, en
  and and_2 (and_2_out, ~state[2], state[1], state[0]);  // AND_Gate
  and and_3 (and_3_out, state[2], ~state[1], ~state[0]);  // AND_Gate
  or or_6 (or_6_out, and_5_out, and_2_out);
  and and_4 (and_4_out, state[2], state[1], state[0]);
  and and_5 (and_5_out, ~state[2], ~state[1], ~state[0]);  // AND_Gate
  or or_7 (or_7_out, and_6_out, and_7_out);
  and and_6 (and_6_out, state[2], ~state[1], state[0]);  // AND_Gate
  Comparator #(.width(4)) comparator_29 (.a(bit_extender_1_out), .b(4'b0100), .eq(match));  // open: gt, lt
  and and_7 (and_7_out, state[2], state[1], ~state[0]);  // AND_Gate
  xnor xnor_1 (xnor_1_out, state[2], state[1], state[0]);
endmodule

module register_setup_guess (
  input  [3:0] I0,
  input  [3:0] I1,
  input  [3:0] I2,
  input  [3:0] I3,
  input  Enter,
  input  Error,
  input  [2:0] state,
  input  clock,
  output [3:0] s0,
  output [3:0] s1,
  output [3:0] s2,
  output [3:0] s3,
  output [3:0] t0,
  output [3:0] t1,
  output [3:0] t2,
  output [3:0] t3
);

  wire and_1_out, and_2_out, and_3_out, and_4_out;

  and and_1 (and_1_out, Enter, ~Error);  // AND_Gate
  and and_2 (and_2_out, and_1_out, ~state[2], ~state[1], ~state[0]);  // AND_Gate
  Register #(.width(4)) register_1 (.D(I0), .en(and_2_out), .Q(s0), .clk(clock));  // open: clr
  Register #(.width(4)) register_2 (.D(I1), .en(and_2_out), .Q(s1), .clk(clock));  // open: clr
  Register #(.width(4)) register_3 (.D(I2), .en(and_2_out), .Q(s2), .clk(clock));  // open: clr
  Register #(.width(4)) register_4 (.D(I3), .en(and_2_out), .Q(s3), .clk(clock));  // open: clr
  and and_3 (and_3_out, and_1_out, ~state[2], state[1], state[0]);  // AND_Gate
  Register #(.width(4)) register_5 (.D(I0), .en(and_3_out), .Q(t0), .clk(clock), .clr(and_4_out));
  Register #(.width(4)) register_6 (.D(I1), .en(and_3_out), .Q(t1), .clk(clock), .clr(and_4_out));
  Register #(.width(4)) register_7 (.D(I2), .en(and_3_out), .Q(t2), .clk(clock), .clr(and_4_out));
  Register #(.width(4)) register_8 (.D(I3), .en(and_3_out), .Q(t3), .clk(clock), .clr(and_4_out));
  and and_4 (and_4_out, ~state[2], ~state[1], state[0]);  // AND_Gate
endmodule

module win_lives_memory (
  input  match,
  input  error,
  input  clock,
  input  [2:0] state,
  output [3:0] wins,
  output [3:0] lives,
  output dead
);

  wire and_1_out, and_2_out, and_3_out, and_4_out;
  wire [2:0] d_ff_1_q, subtractor_1_out;
  wire [3:0] adder_1_out;

  and and_1 (and_1_out, match, ~error);  // AND_Gate
  Adder #(.width(4)) adder_1 (.a(wins), .b(4'b0001), .out(adder_1_out));  // open: cin, cout
  Subtractor #(.width(3)) subtractor_1 (.a(d_ff_1_q), .b(3'b001), .out(subtractor_1_out));  // open: bin, bout
  and and_2 (and_2_out, and_1_out, and_3_out);
  and and_3 (and_3_out, ~state[0], ~state[1], state[2]);  // AND_Gate
  Register #(.width(4)) u_wins (.D(adder_1_out), .en(and_2_out), .Q(wins), .clk(clock));  // open: clr
  and and_4 (and_4_out, ~state[0], ~state[1], ~state[2]);  // AND_Gate
  D_Flip_Flop d_ff_1 (
    .clk(clock), .D(subtractor_1_out[0]), .Q(d_ff_1_q[0]), .preset(and_4_out), .en(and_3_out));  // open: Qn, reset
  D_Flip_Flop d_ff_2 (
    .clk(clock), .D(subtractor_1_out[1]), .Q(d_ff_1_q[1]), .preset(and_4_out), .en(and_3_out));  // open: Qn, reset
  D_Flip_Flop d_ff_3 (
    .clk(clock), .D(subtractor_1_out[2]), .Q(d_ff_1_q[2]), .preset(and_4_out), .en(and_3_out));  // open: Qn, reset
  assign lives = {{1{1'b0}}, d_ff_1_q};  // Bit_Extender bit_extender_1
  and and_5 (dead, d_ff_1_q[0], ~d_ff_1_q[1], ~d_ff_1_q[2]);  // AND_Gate
endmodule

module win_lives_memory_correct (
  input  match,
  input  error,
  input  clock,
  input  [2:0] state,
  output [3:0] wins,
  output [3:0] lives,
  output dead
);

  wire and_1_out, and_2_out, and_3_out, and_4_out, and_5_out, and_7_out, and_8_out, or_1_out;
  wire [2:0] d_ff_1_q, subtractor_1_out;
  wire [3:0] adder_1_out, bit_extender_1_out;

  and and_1 (and_1_out, match, ~error);  // AND_Gate
  Adder #(.width(4)) adder_1 (.a(wins), .b(4'b0001), .out(adder_1_out));  // open: cin, cout
  Subtractor #(.width(3)) subtractor_1 (.a(d_ff_1_q), .b(3'b001), .out(subtractor_1_out));  // open: bin, bout
  and and_2 (and_2_out, and_1_out, and_3_out);
  and and_3 (and_3_out, ~state[0], ~state[1], state[2]);  // AND_Gate
  Register #(.width(4)) u_wins (.D(adder_1_out), .en(and_2_out), .Q(wins), .clk(clock));  // open: clr
  and and_4 (and_4_out, ~state[0], ~state[1], ~state[2]);  // AND_Gate
  D_Flip_Flop d_ff_1 (
    .clk(clock), .D(subtractor_1_out[0]), .Q(d_ff_1_q[0]), .preset(and_4_out), .en(and_3_out));  // open: Qn, reset
  D_Flip_Flop d_ff_2 (
    .clk(clock), .D(subtractor_1_out[1]), .Q(d_ff_1_q[1]), .preset(and_4_out), .en(and_3_out));  // open: Qn, reset
  D_Flip_Flop d_ff_3 (
    .clk(clock), .D(subtractor_1_out[2]), .Q(d_ff_1_q[2]), .preset(and_4_out), .en(and_3_out));  // open: Qn, reset
  assign bit_extender_1_out = {{1{1'b0}}, d_ff_1_q};  // Bit_Extender bit_extender_1
  or or_1 (or_1_out, and_5_out, and_8_out, and_7_out);
  and and_5 (and_5_out, state[0], state[1], ~state[2]);  // AND_Gate
  and and_6 (dead, d_ff_1_q[0], ~d_ff_1_q[1], ~d_ff_1_q[2]);  // AND_Gate
  assign lives = or_1_out ? bit_extender_1_out : 4'bz;  // Controlled_Buffer controlled_buffer_1
  and and_7 (and_7_out, ~state[0], state[1], state[2]);  // AND_Gate
  and and_8 (and_8_out, state[0], ~state[1], state[2]);  // AND_Gate
endmodule
